# Fritzing sketch fritzing-20-dollar-20-minute-esp8266-esp-easy-thingspeak-weather-station (saved by Fritzing 0.9.0b)
breadboards: 1

parts:
  Part1 = Adafruit BME280
  Part2 = OLED Color 0.96 inch 96x64 w microSD [part_number=684]
  U1 = ESP8266 WiFi Module [part_number=ESP8266]
  S2 = Tactile Switch Buttons - 12mm Square [package=tactile-pth-12mm]
  R1 = Resistor [tolerance=±5% resistance=10k package=THT]
  R2 = Resistor [tolerance=±5% resistance=10k package=THT]
  Part3 = FTDI Basic Programmer
  S3 = Toggle Switch [package=THT]

nets:
  VIN: Part1.VIN, Part2.V+, U1.VCC, R1.Pin_0, R2.Pin_0, Part3.POWER
  GND: Part1.GND, Part2.GND, U1.GND, S2.2, S2.4, Part3.GND, S3.COM
  N1: Part1.SCK/SCL, Part2.SCK, U1.GPIO_2
  N2: Part1.CS, Part2.OLED_CS, U1.GPIO_0, S3.L1
  N3: U1.RXD, Part3.TXO
  N4: U1.RST, S2.1, R1.Pin_1
  N5: U1.CH_PD, R2.Pin_1
  N6: U1.TXD, Part3.RXI

custom parts:
  Adafruit BME280: Bosch has stepped up their game with their new BME280 sensor, an environmental sensor with temperature, barometric pressure and humidity! This sensor is great for all sorts of weather/environmental sensing and can even be used in both I2C and SPI! This precision sensor from Bosch is the best low-cost sensing solution for measuring humidity with ±3% accuracy, barometric pressure with ±1 hPa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
  OLED Color 0.96 inch 96x64 w microSD: The visible portion of this OLED measures 0.96" diagonal and contains 96x64 RGB pixels, each one made of red, green and blue OLEDs. Each pixel can be set with 16-bits of resolution for a large range of colors. Because the display uses OLEDs, there is no backlight, and the contrast is very high (black is really black). We picked this display for its excellent color, this is the nicest mini OLED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
  ESP8266 WiFi Module: Generic WiFi Module based on the ESP8266 with onboard PCB antenna and UART communications
  Tactile Switch Buttons - 12mm Square: Medium-sized clicky momentary switches are standard input "buttons" on electronic projects. These work best in a PCB but can be used on a solderless breadboard as shown in this tutorial. The pins are normally open (disconnected) and when the button is pressed they are momentarily closed. They come in a pack of 10, they're pretty handy so you'll want to keep them around. You can find an EAGLE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
